# Fritzing sketch compass-belt (saved by Fritzing 0.9.10b)
stripboards: 1

parts:
  U1 = Vibration Motor- ROB-08449 [package=vibe-motor-10mm]
  IC2 = ULN2803A [package=THT]
  U2 = Vibration Motor- ROB-08449 [package=vibe-motor-10mm]
  U3 = Vibration Motor- ROB-08449 [package=vibe-motor-10mm]
  U4 = Vibration Motor- ROB-08449 [package=vibe-motor-10mm]
  U5 = Vibration Motor- ROB-08449 [package=vibe-motor-10mm]
  U6 = Vibration Motor- ROB-08449 [package=vibe-motor-10mm]
  U7 = Vibration Motor- ROB-08449 [package=vibe-motor-10mm]
  U8 = Vibration Motor- ROB-08449 [package=vibe-motor-10mm]
  U9 = Vibration Motor- ROB-08449 [package=vibe-motor-10mm]
  U10 = Vibration Motor- ROB-08449 [package=vibe-motor-10mm]
  U11 = Vibration Motor- ROB-08449 [package=vibe-motor-10mm]
  U12 = Vibration Motor- ROB-08449 [package=vibe-motor-10mm]
  U13 = Vibration Motor- ROB-08449 [package=vibe-motor-10mm]
  U14 = Vibration Motor- ROB-08449 [package=vibe-motor-10mm]
  U15 = Vibration Motor- ROB-08449 [package=vibe-motor-10mm]
  U16 = Vibration Motor- ROB-08449 [package=vibe-motor-10mm]
  Mod1 = Raspberry Pi Pico
  C2 = Ceramic Capacitor [capacitance=100nF voltage=35V package="100 mil [THT, multilayer]"]
  C3 = Ceramic Capacitor [capacitance=100nF voltage=35V package="100 mil [THT, multilayer]"]
  IC1 = ULN2803A [package=THT]
  C1 = Electrolytic Capacitor [capacitance=220µF voltage=35V package="200 mil [THT, electrolytic]"]

nets:
  N1: U1.+, IC2.Out_1
  N2: U1.-, IC2.COM_-_Common, U2.-, U3.-, U4.-, U5.-, U6.-, U7.-, U8.-, U9.-, U10.-, U11.-, U12.-, U13.-, U14.-, U15.-, U16.-, Mod1.pin_36, C2.0, C3.0, IC1.COM_-_Common, C1.+
  N3: IC2.In_1, Mod1.pin_11
  N4: IC2.In_2, Mod1.pin_10
  N5: IC2.In_3, Mod1.pin_9
  N6: IC2.In_4, Mod1.pin_1
  N7: IC2.In_5, Mod1.pin_7
  N8: IC2.In_6, Mod1.pin_6
  N9: IC2.In_7, Mod1.pin_5
  N10: IC2.In_8, Mod1.pin_4
  N11: IC2.0V, Mod1.pin_3, Mod1.pin_8, Mod1.pin_13, Mod1.pin_18, Mod1.pin_23, Mod1.pin_28, Mod1.pin_33, Mod1.pin_38, C2.1, C3.1, IC1.0V, C1.-
  N12: IC2.Out_8, U8.+
  N13: IC2.Out_7, U7.+
  N14: IC2.Out_6, U6.+
  N15: IC2.Out_5, U5.+
  N16: IC2.Out_4, U4.+
  N17: IC2.Out_3, U3.+
  N18: IC2.Out_2, U2.+
  N19: U9.+, IC1.Out_1
  N20: U10.+, IC1.Out_2
  N21: U11.+, IC1.Out_3
  N22: U12.+, IC1.Out_4
  N23: U13.+, IC1.Out_5
  N24: U14.+, IC1.Out_6
  N25: U15.+, IC1.Out_7
  N26: U16.+, IC1.Out_8
  N27: Mod1.pin_12, IC1.In_4
  N28: Mod1.pin_14, IC1.In_8
  N29: Mod1.pin_15, IC1.In_7
  N30: Mod1.pin_16, IC1.In_6
  N31: Mod1.pin_17, IC1.In_5
  N32: Mod1.pin_19, IC1.In_3
  N33: Mod1.pin_20, IC1.In_2
  N34: Mod1.pin_21, IC1.In_1

custom parts:
  Raspberry Pi Pico: Raspberry Pi Pico. Based around the RP2040 microcontroller the Pico is a low cost microcontroller device bringing Raspberry Pi quality, cost, and easy of use to the microcontroller space. Jan 2021, Split part in to two versions: tht (this one) and SMD. This one will drill holes for a .1 in header in pcb to allow plugging in the module as well as providing pads to solder the module to the top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
